# Fritzing sketch remote (saved by Fritzing 1.0.1rc)
circuit board: 2.09424cm x 3.05769cm
breadboards: 1

parts:
  AT85 = ATTINY13 [package=dip]
  0_1µF = Capacitor [package=cap-pth-small]
  STX882 = mystery part, 3 pins [chip_label=?]
  220Ω = Resistor [tolerance=±5% power=0.25 resistance=220 package=THT]
  LED1 = LED - 5mm [color="Red (633nm)" current=0.030 package="5 mm [THT]"]
  Switch = Toggle Switch [package=THT]
  GND = mystery part, 2 pins [chip_label=?]
  ₿ = Momentary Switch [package=tactile-pth]

nets:
  N1: AT85.PB3(ADC3), STX882.pin1
  N2: AT85.GND, 0_1µF.1, STX882.pin3, LED1.cathode, Switch.COM, ₿.1
  N3: AT85.PB0(MOSI), Switch.L1
  N4: AT85.PB2(SCK_ADC1), 220Ω.Pin_0
  N5: AT85.VCC, 0_1µF.2, STX882.pin2, GND.pin2
  N6: 220Ω.Pin_1, LED1.anode
  N7: GND.pin1, ₿.4

notes:
  433MHz
  Remote V1
